// Logisim project hw3.circ as structural Verilog: 5 circuits, main circuit part1
module part1 (
  input  A,
  input  B,
  input  Carry_In,
  output Answer,
  output Carry_Out
);

  wire and_1_out, and_2_out, and_3_out, and_4_out, and_5_out, nor_1_out, not_1_out, not_2_out, xor_1_out;

  xor xor_1 (xor_1_out, A, B);
  and and_1 (and_1_out, A, B);
  nor nor_1 (nor_1_out, A, B);
  not not_1 (not_1_out, Carry_In);
  not not_2 (not_2_out, nor_1_out);
  and and_2 (and_2_out, xor_1_out, not_1_out);
  and and_3 (and_3_out, and_1_out, Carry_In);
  and and_4 (and_4_out, nor_1_out, Carry_In);
  and and_5 (and_5_out, not_2_out, Carry_In);
  or or_1 (Carry_Out, and_1_out, and_5_out);
  or or_2 (Answer, and_2_out, and_3_out, and_4_out);
endmodule

module part2 (
  input  Carry_In,
  input  [3:0] A,
  input  [3:0] B,
  output [3:0] Answer,
  output Carry_Out
);

  wire part1_1_carry_out, part1_2_carry_out, part1_3_carry_out;

  part1 part1_1 (.A(A[0]), .B(B[0]), .Carry_In(Carry_In), .Answer(Answer[0]), .Carry_Out(part1_1_carry_out));
  part1 part1_2 (.A(A[1]), .B(B[1]), .Carry_In(part1_1_carry_out), .Answer(Answer[1]), .Carry_Out(part1_2_carry_out));
  part1 part1_3 (.A(A[2]), .B(B[2]), .Carry_In(part1_2_carry_out), .Answer(Answer[2]), .Carry_Out(part1_3_carry_out));
  part1 part1_4 (.A(A[3]), .B(B[3]), .Carry_In(part1_3_carry_out), .Answer(Answer[3]), .Carry_Out(Carry_Out));
endmodule

module part3 (
  input  S2,
  input  S1,
  input  S0,
  input  [3:0] A,
  input  [3:0] B,
  output [3:0] out_6
);

  wire or_1_out;
  wire [0:0] isMultipleOf4;
  wire [3:0] Addition, MultiplyBy2, NAND, Negation, NOR, not_1_out, not_2_out, Subtraction, XOR;

  assign not_1_out = ~B;  // NOT_Gate not_1, 4 bits wide
  assign not_2_out = ~A;  // NOT_Gate not_2, 4 bits wide
  part2 part2_1 (.Carry_In(1'b0), .A(A), .B(B), .Answer(Addition));  // open: Carry_Out
  part2 part2_2 (.Carry_In(1'b1), .A(A), .B(not_1_out), .Answer(Subtraction));  // open: Carry_Out
  not not_3 (isMultipleOf4[0], or_1_out);
  or or_1 (or_1_out, A[0], A[1]);
  part2 part2_3 (.Carry_In(1'b0), .A(not_2_out), .B(4'b0001), .Answer(Negation));  // open: Carry_Out
  part2 part2_4 (.Carry_In(1'b0), .A(A), .B(A), .Answer(MultiplyBy2));  // open: Carry_Out
  assign NAND = ~(A & B);  // NAND_Gate nand_1, 4 bits wide
  assign NOR = ~(A | B);  // NOR_Gate nor_1, 4 bits wide
  assign XOR = A ^ B;  // XOR_Gate xor_1, 4 bits wide
  Multiplexer #(.select(3), .width(4), .disabled(0)) multiplexer_1 (
    .in0(Addition), .in1(Subtraction), .in2({3'b000, isMultipleOf4[0]}), .in3(Negation), .in4(MultiplyBy2),
    .in5(NAND), .in6(NOR), .in7(XOR), .out(out_6), .sel({S2, S1, S0}));  // open: en

  // Other names for the same wires on the sheet: Output[3:0] = out_6; Selector[2:0] = {S2, S1, S0}

  // Notes on the sheet:
  //   000 Addition
  //   001 Subtraction
  //   010 isMultipleOf4
  //   011 Negation
  //   100 MultiplyBy2
  //   101 NAND
  //   110 NOR
  //   111 XOR
endmodule

module part4 (
  input  S2,
  input  S1,
  input  S0,
  input  [15:0] A,
  input  [15:0] B,
  output [15:0] out_6
);

  wire or_1_out;
  wire [0:0] isMultipleOf4;
  wire [15:0] Addition, NAND, Negation, NOR, not_1_out, not_2_out, Subtraction, XOR;

  assign not_1_out = ~B;  // NOT_Gate not_1, 16 bits wide
  assign not_2_out = ~A;  // NOT_Gate not_2, 16 bits wide
  _16bitadder u_16bitadder_1 (.Carry_in(1'b0), .A(A), .B(B), .Answer(Addition));  // open: Carry_Out
  _16bitadder u_16bitadder_2 (.Carry_in(1'b1), .A(A), .B(not_1_out), .Answer(Subtraction));  // open: Carry_Out
  not not_3 (isMultipleOf4[0], or_1_out);
  or or_1 (or_1_out, A[0], A[1]);
  _16bitadder u_16bitadder_3 (.Carry_in(1'b1), .A(not_2_out), .B({16{1'b0}}), .Answer(Negation));  // open: Carry_Out
  assign NAND = ~(A & B);  // NAND_Gate nand_1, 16 bits wide
  assign NOR = ~(A | B);  // NOR_Gate nor_1, 16 bits wide
  assign XOR = A ^ B;  // XOR_Gate xor_1, 16 bits wide
  Multiplexer #(.select(3), .width(16), .disabled(0)) multiplexer_1 (
    .in0(Addition), .in1(Subtraction), .in2({{15{1'b0}}, isMultipleOf4[0]}), .in3(Negation),
    .in4({A[12:0], 3'b000}), .in5(NAND), .in6(NOR), .in7(XOR), .out(out_6), .sel({S2, S1, S0}));  // open: en

  // Other names for the same wires on the sheet: MultiplyBy8[15:3] = A[12:0]; Output[15:0] = out_6;
  //   Selector[2:0] = {S2, S1, S0}

  // Notes on the sheet:
  //   000 Addition
  //   001 Subtraction
  //   010 isMultipleOf4
  //   011 Negation
  //   100 MultiplyBy8
  //   101 NAND
  //   110 NOR
  //   111 XOR
endmodule

module _16bitadder (
  input  Carry_in,
  input  [15:0] A,
  input  [15:0] B,
  output [15:0] Answer,
  output Carry_Out
);

  wire part2_1_carry_out, part2_2_carry_out, part2_3_carry_out;

  part2 part2_1 (.Carry_In(Carry_in), .A(A[3:0]), .B(B[3:0]), .Answer(Answer[3:0]), .Carry_Out(part2_1_carry_out));
  part2 part2_2 (
    .Carry_In(part2_1_carry_out), .A(A[7:4]), .B(B[7:4]), .Answer(Answer[7:4]), .Carry_Out(part2_2_carry_out));
  part2 part2_3 (
    .Carry_In(part2_2_carry_out), .A(A[11:8]), .B(B[11:8]), .Answer(Answer[11:8]),
    .Carry_Out(part2_3_carry_out));
  part2 part2_4 (
    .Carry_In(part2_3_carry_out), .A(A[15:12]), .B(B[15:12]), .Answer(Answer[15:12]), .Carry_Out(Carry_Out));
endmodule
